// Logisim project splitter.circ as structural Verilog: 1 circuit, main circuit main
module main (
  input  A,
  input  B,
  input  C,
  output [1:0] S,
  output [1:0] E
);

  assign E = {{1{1'b1}}, C};  // Bit_Extender bit_extender_1

  assign S = {B, A};
endmodule
